# Fritzing sketch Rangkaian Alat Kendali Kualitas Udara (saved by Fritzing 0.9.3b)
breadboards: 1

parts:
  LCD3 = LCD screen
  Part1 = Arduino Uno (Rev3) - ICSP
  LCM1602_IIC2 = LCM1602 IIC [part_number="LCM1602 IIC" chip_label="LCM1602 IIC" package="DIP (Dual Inline) [THT]"]
  Mod1 = MQ-7 breakout
  U1 = Sharp Dust Sensor [part_number=GP2Y1010AU0F]
  R1 = Resistor [tolerance=±5% resistance=220 package=THT]  # not connected
  C1 = Electrolytic Capacitor [capacitance=1µF package="100 mil [THT, electrolytic]"]
  LED1 = LED - 5mm [color="Red (633nm)" package="5 mm [THT]"]
  U2 = ESP32S-HiLetgo [part_number=ESP32S-HiLetgo]
  R2 = Resistor [tolerance=±5% resistance=220 package=THT]
  F2 = Fan - Ventilador [package=THT]
  F3 = Fan - Ventilador [package=THT]
  F4 = Fan - Ventilador [package=THT]
  F5 = Fan - Ventilador [package=THT]
  Power_plug1 = Power plug
  A2 = 2 channel relay module [package=THT]

nets:
  VSS: LCD3.VSS, LCM1602_IIC2.VSS
  VDD: LCD3.VDD, LCM1602_IIC2.VDD
  N1: LCD3.V0, LCM1602_IIC2.V0
  N2: LCD3.RS, LCM1602_IIC2.RS
  N3: LCD3.R/W, LCM1602_IIC2.RW
  N4: LCD3.E, LCM1602_IIC2.E
  N5: LCD3.DB0, LCM1602_IIC2.D0
  N6: LCD3.DB1, LCM1602_IIC2.D1
  N7: LCD3.DB2, LCM1602_IIC2.D2
  N8: LCD3.DB3, LCM1602_IIC2.D3
  N9: LCD3.DB4, LCM1602_IIC2.D4
  N10: LCD3.DB5, LCM1602_IIC2.D5
  N11: LCD3.DB6, LCM1602_IIC2.D6
  N12: LCD3.DB7, LCM1602_IIC2.D7
  N13: LCD3.LED+, LCM1602_IIC2.A
  N14: LCD3.LED-, LCM1602_IIC2.K
  N15: Part1.A0, U1.Vo
  N16: Part1.A1, Mod1.AO
  N17: Part1.A4/SDA, LCM1602_IIC2.SDA
  N18: Part1.A5/SCL, LCM1602_IIC2.SCL
  N19: Part1.D2, U2.GPIO17
  N20: Part1.D3_PWM, U2.GPIO16
  N21: Part1.D7, U1.LED
  5V: Part1.5V, U1.VCC, R2.Pin_1, A2.pin_13
  GND: Part1.GND, U1.LED-GND, U1.S-GND, C1.+, U2.GND, A2.pin_14
  N22: LCM1602_IIC2.LED_A, LCM1602_IIC2.LED_B
  N23: LED1.cathode, U2.GPIO15
  N24: LED1.anode, R2.Pin_0
  N25: U2.GPIO2, A2.pin_16
  N26: U2.GPIO4, A2.pin_15
  5V_2: F2.5V, F3.5V, A2.pin_4
  GND_2: F2.GND, F3.GND, F4.GND, F5.GND, Power_plug1.GND
  5V_3: F4.5V, F5.5V, A2.pin_1
  N27: Power_plug1.VCC, A2.pin_2

custom parts:
  LCM1602 IIC: I2C-Module to use a 1602 or 2004 LCD on with the wire.h libory Serial LCD Modul
  MQ-7 breakout: MQ-5 gas sensor
  Sharp Dust Sensor: Sharp GP2Y1010AU0F Dust Sensor
  ESP32S-HiLetgo: HiLetgo ESP-WROOM-32 ESP32 ESP-32S Development Board 2.4GHz Dual-Mode WiFi + Bluetooth Dual Cores Microcontroller The ESP32 integrated with Antenna switches, RF Balun, power amplifiers, low-noise amplifiers, filters, and management modules, and the entire solution occupies the least area of PCB. 2.4 GHz Wi-Fi plus Bluetooth dual-mode chip, with TSMC Ultra-low power consumption 40nm technology,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
  Fan - Ventilador: Ventilador de 2 pines, se encuentra comunmente en computadoras de escritorio
  2 channel relay module: 2 channel Relay Module 5V 12V 24V High and Low Level Trigger Relay Control With Optocoupler Two Way relays DC 5 V 12 V 24 V Volt.
